// Logisim project cpu.circ as structural Verilog: 1 circuit, main circuit cpu
module cpu (
  input  clk,
  input  [31:0] Instruction,
  input  [31:0] MemReadData,
  output [31:0] MemAddress,
  output [31:0] ProgramCounter,
  output [31:0] ra,
  output [31:0] sp,
  output [31:0] t0,
  output [31:0] t1,
  output [31:0] t2,
  output [31:0] s0,
  output [31:0] s1,
  output [31:0] a0,
  output [3:0] MemWriteMask,
  output [31:0] MemWriteData,
  output [4:0] ReadIndex1,
  output [4:0] ReadIndex2,
  output [4:0] WriteIndex,
  output [31:0] WriteData,
  output [31:0] PCInput,
  output [31:0] ReadData1,
  output [31:0] ReadData2,
  output ASel,
  output BSel,
  output [3:0] out_25,
  output BrEq,
  output [31:0] ALU_RES,
  output BrLt,
  output [4:0] I_rd,
  output [31:0] ALU_A,
  output [31:0] ALU_B,
  output PCSel,
  output [4:0] I_rs1,
  output [31:0] Imm
);

  wire BrUn, Imm_I_Type, or_1_out, or_2_out, R_Type, RegWEn;
  wire [2:0] ImmSel;
  wire [31:0] Gen_Immediate, PC_PLUS_4;

  Adder #(.width(32)) adder_1 (.a(ProgramCounter), .b(32'h4), .out(PC_PLUS_4));  // open: cin, cout
  or or_1 (or_1_out, Imm_I_Type, R_Type);
  Multiplexer #(.width(5)) multiplexer_1 (.in1(Instruction[24:20]), .out(ReadIndex2), .sel(R_Type));  // open: in0
  Multiplexer #(.width(5)) multiplexer_2 (.in1(Instruction[11:7]), .out(WriteIndex), .sel(or_2_out));  // open: in0
  or or_2 (or_2_out, Imm_I_Type, R_Type);
  Register #(.width(32)) PC (.D(PCInput), .clk(clk), .Q(ProgramCounter));  // open: en, clr
  Multiplexer #(.width(32)) multiplexer_3 (.in0(PC_PLUS_4), .in1(ALU_RES), .out(PCInput), .sel(PCSel));
  Comparator #(.mode("unsigned"), .width(7)) comparator_1 (
    .a(Instruction[6:0]), .b(7'b0010011), .eq(Imm_I_Type));  // open: gt, lt
  Comparator #(.mode("unsigned"), .width(7)) comparator_2 (
    .a(Instruction[6:0]), .b(7'b0110011), .eq(R_Type));  // open: gt, lt
  Multiplexer #(.width(5)) multiplexer_4 (.in1(Instruction[19:15]), .out(ReadIndex1), .sel(or_1_out));  // open: in0
  Multiplexer #(.width(32)) multiplexer_5 (.in0(ReadData1), .in1(ProgramCounter), .out(ALU_A), .sel(ASel));
  Multiplexer #(.width(32)) multiplexer_6 (.in0(ReadData2), .in1(Imm), .out(ALU_B), .sel(BSel));
  control_logic control_logic_1 (
    .Instruction(Instruction), .BrEq(BrEq), .BrLt(BrLt), .PCSel(PCSel), .RegWEn(RegWEn), .ImmSel(ImmSel),
    .BrUn(BrUn), .ASel(ASel), .BSel(BSel), .ALUSel(out_25));  // open: MemWEn, WBSel
  imm_gen imm_gen_1 (.Instruction(Instruction), .ImmSel(ImmSel), .Immediate(Gen_Immediate));
  regfile regfile_1 (
    .ReadIndex1(ReadIndex1), .ReadIndex2(ReadIndex2), .WriteIndex(WriteIndex), .WriteData(ALU_RES),
    .RegWEn(RegWEn), .clk(clk), .ra(ra), .sp(sp), .t0(t0), .t1(t1), .t2(t2), .s0(s0), .s1(s1), .a0(a0),
    .ReadData1(ReadData1), .ReadData2(ReadData2));
  Multiplexer #(.width(32)) multiplexer_7 (.in0(Gen_Immediate), .in1(Gen_Immediate), .out(Imm), .sel(PCSel));
  alu alu_1 (.A(ALU_A), .B(ALU_B), .ALUSel(out_25), .ALUResult(ALU_RES));
  branch_comp branch_comp_1 (.BrData1(ReadData1), .BrData2(ReadData2), .BrUn(BrUn), .BrEq(BrEq), .BrLt(BrLt));
  // partial_store partial_store_1: pin names not known
  // partial_load partial_load_1: pin names not known

  assign I_rd = Instruction[11:7];
  assign I_rs1 = Instruction[19:15];
  assign WriteData = ALU_RES;

  // Other names for the same wires on the sheet: ALUSel[3:0] = out_25; Immediate[31:0] = Imm;
  //   Opcode[6:0] = Instruction[6:0]; Instruction31_7[24:0] = Instruction[31:7]; rd[4:0] = Instruction[11:7];
  //   I_funct3[2:0] = Instruction[14:12]; rs1[4:0] = Instruction[19:15]; rs2[4:0] = Instruction[24:20];
  //   funct7[6:0] = Instruction[31:25]; ProgramCounterInput[31:0] = PCInput

  // Notes on the sheet:
  //   To IMEM
  //   IMEM (do **NOT** move this)
  //   From IMEM
  //   Inputs/Outputs for testing. Do **NOT** move these.
  //   It is OK to move the PC, RegFile, ALU, MEM, Branch Comp, Imm Gen, Partial Load, Partial Store and Control Logic to wherever is most convenient for you when constructing your CPU, and to delete this text
  //   To DMEM
  //   DMEM (do **NOT** move this)
  //   From DMEM
endmodule
